// Logisim project TrisRevA.circ as structural Verilog: 3 circuits, main circuit main
module main (
);

  wire button_1_out, button_2_out, button_3_out, button_4_out, button_5_out, button_6_out, button_7_out,
       button_8_out, button_9_out, or_1_out, or_2_out, or_3_out, or_4_out, or_5_out, or_6_out, or_7_out,
       or_8_out, or_9_out, px_driver_1_l1, px_driver_1_l2, px_driver_2_l1, px_driver_2_l2, px_driver_3_l1,
       px_driver_3_l2, px_driver_4_l1, px_driver_4_l2, px_driver_5_l1, px_driver_5_l2, px_driver_6_l1,
       px_driver_6_l2, px_driver_7_l1, px_driver_7_l2, px_driver_8_l1, px_driver_8_l2, px_driver_9_l1,
       px_driver_9_l2, RESET_out, t_ff_1_q, xor_1_out;

  Button button_1 (.out(button_1_out));
  Button button_2 (.out(button_2_out));
  Button button_3 (.out(button_3_out));
  Button button_4 (.out(button_4_out));
  Button button_5 (.out(button_5_out));
  Button button_6 (.out(button_6_out));
  Button RESET (.out(RESET_out));
  Button button_7 (.out(button_7_out));
  Button button_8 (.out(button_8_out));
  Button button_9 (.out(button_9_out));
  T_Flip_Flop t_ff_1 (.clk(RESET_out), .T(1'b1), .Q(t_ff_1_q), .preset(1'b0), .reset(1'b0), .en(1'b1));  // open: Qn
  PX_driver px_driver_1 (.IN(button_2_out), .T(xor_1_out), .L1(px_driver_1_l1), .L2(px_driver_1_l2), .RESET(RESET_out));
  PX_driver px_driver_2 (.IN(button_1_out), .T(xor_1_out), .L1(px_driver_2_l1), .L2(px_driver_2_l2), .RESET(RESET_out));
  PX_driver px_driver_3 (.IN(button_7_out), .T(xor_1_out), .L1(px_driver_3_l1), .L2(px_driver_3_l2), .RESET(RESET_out));
  PX_driver px_driver_4 (.IN(button_4_out), .T(xor_1_out), .L1(px_driver_4_l1), .L2(px_driver_4_l2), .RESET(RESET_out));
  PX_driver px_driver_5 (.IN(button_3_out), .T(xor_1_out), .L1(px_driver_5_l1), .L2(px_driver_5_l2), .RESET(RESET_out));
  PX_driver px_driver_6 (.IN(button_8_out), .T(xor_1_out), .L1(px_driver_6_l1), .L2(px_driver_6_l2), .RESET(RESET_out));
  PX_driver px_driver_7 (.IN(button_5_out), .T(xor_1_out), .L1(px_driver_7_l1), .L2(px_driver_7_l2), .RESET(RESET_out));
  PX_driver px_driver_8 (.IN(button_6_out), .T(xor_1_out), .L1(px_driver_8_l1), .L2(px_driver_8_l2), .RESET(RESET_out));
  PX_driver px_driver_9 (.IN(button_9_out), .T(xor_1_out), .L1(px_driver_9_l1), .L2(px_driver_9_l2), .RESET(RESET_out));
  LED led_1 (.in(px_driver_1_l1));
  LED led_2 (.in(px_driver_1_l1));
  LED led_3 (.in(px_driver_4_l1));
  LED led_4 (.in(px_driver_4_l1));
  LED led_5 (.in(px_driver_7_l1));
  LED led_6 (.in(px_driver_7_l1));
  LED led_7 (.in(px_driver_2_l1));
  LED led_8 (.in(px_driver_1_l2));
  LED led_9 (.in(px_driver_2_l2));
  LED led_10 (.in(px_driver_2_l1));
  LED led_11 (.in(px_driver_1_l2));
  LED led_12 (.in(px_driver_2_l2));
  LED led_13 (.in(px_driver_5_l2));
  LED led_14 (.in(px_driver_5_l1));
  LED led_15 (.in(px_driver_4_l2));
  LED led_16 (.in(px_driver_4_l2));
  LED led_17 (.in(px_driver_5_l1));
  LED led_18 (.in(px_driver_5_l2));
  LED led_19 (.in(px_driver_8_l1));
  LED led_20 (.in(px_driver_8_l2));
  LED led_21 (.in(px_driver_7_l2));
  LED led_22 (.in(px_driver_7_l2));
  LED led_23 (.in(px_driver_8_l2));
  LED led_24 (.in(px_driver_8_l1));
  LED led_25 (.in(px_driver_3_l2));
  LED led_26 (.in(px_driver_3_l1));
  LED led_27 (.in(px_driver_3_l1));
  LED led_28 (.in(px_driver_3_l2));
  LED led_29 (.in(px_driver_6_l2));
  LED led_30 (.in(px_driver_6_l1));
  LED led_31 (.in(px_driver_6_l1));
  LED led_32 (.in(px_driver_6_l2));
  LED led_33 (.in(px_driver_9_l2));
  LED led_34 (.in(px_driver_9_l1));
  LED led_35 (.in(px_driver_9_l2));
  LED led_36 (.in(px_driver_9_l1));
  or or_1 (or_1_out, px_driver_1_l1, px_driver_1_l2);
  or or_2 (or_2_out, px_driver_2_l1, px_driver_2_l2);
  or or_3 (or_3_out, px_driver_3_l1, px_driver_3_l2);
  or or_4 (or_4_out, px_driver_4_l2, px_driver_4_l1);
  or or_5 (or_5_out, px_driver_5_l1, px_driver_5_l2);
  or or_6 (or_6_out, px_driver_6_l1, px_driver_6_l2);
  or or_7 (or_7_out, px_driver_7_l1, px_driver_7_l2);
  or or_8 (or_8_out, px_driver_8_l1, px_driver_8_l2);
  or or_9 (or_9_out, px_driver_9_l1, px_driver_9_l2);
  ExactlyOne xor_1 (
    .out(xor_1_out), .in0(or_1_out), .in1(or_2_out), .in2(or_3_out), .in3(or_4_out), .in4(or_5_out),
    .in5(or_6_out), .in6(or_7_out), .in7(or_8_out), .in8(or_9_out), .in9(t_ff_1_q));
endmodule

module PX_driver (
  input  IN,
  input  T,
  input  RESET,
  output L1,
  output L2
);

  wire and_1_out, and_2_out, demultiplexer_1_out0, demultiplexer_1_out1, latch_s_r_3_nq, or_1_out;

  Demultiplexer #(.enable("false")) demultiplexer_1 (
    .out0(demultiplexer_1_out0), .out1(demultiplexer_1_out1), .in(IN), .sel(T));
  and and_1 (and_1_out, demultiplexer_1_out0, latch_s_r_3_nq);
  and and_2 (and_2_out, demultiplexer_1_out1, latch_s_r_3_nq);
  latch_S_R latch_s_r_1 (.S(and_1_out), .R(RESET), .Q(L1));  // open: nQ
  latch_S_R latch_s_r_2 (.S(and_2_out), .R(RESET), .Q(L2));  // open: nQ
  or or_1 (or_1_out, L1, L2);
  latch_S_R latch_s_r_3 (.S(or_1_out), .R(RESET), .nQ(latch_s_r_3_nq));  // open: Q
endmodule

module latch_S_R (
  input  S,
  input  R,
  output Q,
  output nQ
);

  nor nor_1 (nQ, S, Q);
  nor nor_2 (Q, nQ, R);
endmodule
