// Logisim project TrisRevB.circ as structural Verilog: 3 circuits, main circuit main
module main (
);

  wire button_1_out, button_2_out, button_3_out, button_4_out, button_5_out, button_6_out, button_7_out,
       button_8_out, button_9_out, px_driver_1_l1, px_driver_1_l2, px_driver_1_or, px_driver_2_l1,
       px_driver_2_l2, px_driver_2_or, px_driver_3_l1, px_driver_3_l2, px_driver_3_or, px_driver_4_l1,
       px_driver_4_l2, px_driver_4_or, px_driver_5_l1, px_driver_5_l2, px_driver_5_or, px_driver_6_l1,
       px_driver_6_l2, px_driver_6_or, px_driver_7_l1, px_driver_7_l2, px_driver_7_or, px_driver_8_l1,
       px_driver_8_l2, px_driver_8_or, px_driver_9_l1, px_driver_9_l2, px_driver_9_or, RESET_out, t_ff_1_q,
       xor_1_out;

  Button button_1 (.out(button_1_out));
  Button button_2 (.out(button_2_out));
  Button button_3 (.out(button_3_out));
  Button button_4 (.out(button_4_out));
  Button button_5 (.out(button_5_out));
  Button button_6 (.out(button_6_out));
  Button RESET (.out(RESET_out));
  Button button_7 (.out(button_7_out));
  Button button_8 (.out(button_8_out));
  Button button_9 (.out(button_9_out));
  T_Flip_Flop t_ff_1 (.clk(RESET_out), .T(1'b1), .Q(t_ff_1_q), .preset(1'b0), .reset(1'b0), .en(1'b1));  // open: Qn
  PX_driver px_driver_1 (
    .IN(button_2_out), .T(xor_1_out), .L1(px_driver_1_l1), .L2(px_driver_1_l2), .RESET(RESET_out),
    .OR(px_driver_1_or));
  PX_driver px_driver_2 (
    .IN(button_1_out), .T(xor_1_out), .L1(px_driver_2_l1), .L2(px_driver_2_l2), .RESET(RESET_out),
    .OR(px_driver_2_or));
  PX_driver px_driver_3 (
    .IN(button_7_out), .T(xor_1_out), .L1(px_driver_3_l1), .L2(px_driver_3_l2), .RESET(RESET_out),
    .OR(px_driver_3_or));
  PX_driver px_driver_4 (
    .IN(button_4_out), .T(xor_1_out), .L1(px_driver_4_l1), .L2(px_driver_4_l2), .RESET(RESET_out),
    .OR(px_driver_4_or));
  PX_driver px_driver_5 (
    .IN(button_3_out), .T(xor_1_out), .L1(px_driver_5_l1), .L2(px_driver_5_l2), .RESET(RESET_out),
    .OR(px_driver_5_or));
  PX_driver px_driver_6 (
    .IN(button_8_out), .T(xor_1_out), .L1(px_driver_6_l1), .L2(px_driver_6_l2), .RESET(RESET_out),
    .OR(px_driver_6_or));
  PX_driver px_driver_7 (
    .IN(button_5_out), .T(xor_1_out), .L1(px_driver_7_l1), .L2(px_driver_7_l2), .RESET(RESET_out),
    .OR(px_driver_7_or));
  PX_driver px_driver_8 (
    .IN(button_6_out), .T(xor_1_out), .L1(px_driver_8_l1), .L2(px_driver_8_l2), .RESET(RESET_out),
    .OR(px_driver_8_or));
  PX_driver px_driver_9 (
    .IN(button_9_out), .T(xor_1_out), .L1(px_driver_9_l1), .L2(px_driver_9_l2), .RESET(RESET_out),
    .OR(px_driver_9_or));
  _7_Segment_Display u_7_segment_display_1 (
    .g(px_driver_1_l1), .f(px_driver_1_or), .a(px_driver_1_l2), .b(px_driver_1_or), .e(px_driver_1_or),
    .d(px_driver_1_l2), .c(px_driver_1_or));  // open: dp
  _7_Segment_Display u_7_segment_display_2 (
    .g(px_driver_2_l1), .f(px_driver_2_or), .a(px_driver_2_l2), .b(px_driver_2_or), .e(px_driver_2_or),
    .d(px_driver_2_l2), .c(px_driver_2_or));  // open: dp
  _7_Segment_Display u_7_segment_display_3 (
    .g(px_driver_4_l1), .f(px_driver_4_or), .a(px_driver_4_l2), .b(px_driver_4_or), .e(px_driver_4_or),
    .d(px_driver_4_l2), .c(px_driver_4_or));  // open: dp
  _7_Segment_Display u_7_segment_display_4 (
    .g(px_driver_5_l1), .f(px_driver_5_or), .a(px_driver_5_l2), .b(px_driver_5_or), .e(px_driver_5_or),
    .d(px_driver_5_l2), .c(px_driver_5_or));  // open: dp
  _7_Segment_Display u_7_segment_display_5 (
    .g(px_driver_8_l1), .f(px_driver_8_or), .a(px_driver_8_l2), .b(px_driver_8_or), .e(px_driver_8_or),
    .d(px_driver_8_l2), .c(px_driver_8_or));  // open: dp
  _7_Segment_Display u_7_segment_display_6 (
    .g(px_driver_7_l1), .f(px_driver_7_or), .a(px_driver_7_l2), .b(px_driver_7_or), .e(px_driver_7_or),
    .d(px_driver_7_l2), .c(px_driver_7_or));  // open: dp
  _7_Segment_Display u_7_segment_display_7 (
    .g(px_driver_3_l1), .f(px_driver_3_or), .a(px_driver_3_l2), .b(px_driver_3_or), .e(px_driver_3_or),
    .d(px_driver_3_l2), .c(px_driver_3_or));  // open: dp
  _7_Segment_Display u_7_segment_display_8 (
    .g(px_driver_6_l1), .f(px_driver_6_or), .a(px_driver_6_l2), .b(px_driver_6_or), .e(px_driver_6_or),
    .d(px_driver_6_l2), .c(px_driver_6_or));  // open: dp
  _7_Segment_Display u_7_segment_display_9 (
    .g(px_driver_9_l1), .f(px_driver_9_or), .a(px_driver_9_l2), .b(px_driver_9_or), .e(px_driver_9_or),
    .d(px_driver_9_l2), .c(px_driver_9_or));  // open: dp
  xor xor_1 (xor_1_out, px_driver_1_or, px_driver_2_or, px_driver_3_or, px_driver_4_or, px_driver_5_or, px_driver_6_or, px_driver_7_or, px_driver_8_or, px_driver_9_or, t_ff_1_q);
endmodule

module PX_driver (
  input  IN,
  input  T,
  input  RESET,
  output L1,
  output OR,
  output L2
);

  wire and_1_out, and_2_out, demultiplexer_1_out0, demultiplexer_1_out1, latch_s_r_3_nq;

  Demultiplexer #(.enable("false")) demultiplexer_1 (
    .out0(demultiplexer_1_out0), .out1(demultiplexer_1_out1), .in(IN), .sel(T));
  and and_1 (and_1_out, demultiplexer_1_out0, latch_s_r_3_nq);
  and and_2 (and_2_out, demultiplexer_1_out1, latch_s_r_3_nq);
  latch_S_R latch_s_r_1 (.S(and_1_out), .R(RESET), .Q(L1));  // open: nQ
  latch_S_R latch_s_r_2 (.S(and_2_out), .R(RESET), .Q(L2));  // open: nQ
  or or_1 (OR, L1, L2);
  latch_S_R latch_s_r_3 (.S(OR), .R(RESET), .nQ(latch_s_r_3_nq));  // open: Q
endmodule

module latch_S_R (
  input  S,
  input  R,
  output Q,
  output nQ
);

  nor nor_1 (nQ, S, Q);
  nor nor_2 (Q, nQ, R);
endmodule
